# Fritzing sketch rgmatrix_bb (saved by Fritzing 0.9.3b)
stripboards: 1

parts:
  J1 = shrouded pin header, 26 pins [form="♂ (shrouded male)"]
  JACK1 = 2.1mm DC Barrel Jack
  J7 = male pin header, 8 pins [form="♂ (male)"]
  J2 = male pin header, 3 pins [form="♂ (male)"]
  J8 = male pin header, 3 pins [form="♂ (male)"]  # not connected
  J9 = male pin header, 1 pin [form="♂ (male)"]
  J10 = male pin header, 1 pin [form="♂ (male)"]
  J11 = male pin header, 8 pins [form="♂ (male)"]
  J12 = male pin header, 6 pins [form="♂ (male)"]

nets:
  N1: J1.pin1, J2.pin2, J12.pin6
  N2: J1.pin6, J7.pin5
  N3: J1.pin8, J11.pin8
  N4: J1.pin10, J7.pin4
  N5: J1.pin12, J11.pin1
  N6: J1.pin15, J11.pin2
  N7: J1.pin16, J11.pin5
  N8: J1.pin17, J10.pin1
  N9: J1.pin18, J11.pin6
  N10: J1.pin19, J11.pin7
  N11: J1.pin21, J9.pin1
  N12: J1.pin22, J12.pin3
  N13: J1.pin23, J12.pin4
  N14: J1.pin24, JACK1.sleeve, J12.pin2
  N15: J1.pin26, J2.pin3, J12.pin1
  N16: JACK1.center, JACK1.switch, J2.pin1
  N17: J7.pin1, J7.pin2, J7.pin6, J7.pin7, J7.pin8
  N18: J7.pin3, J11.pin3

custom parts:
  2.1mm DC Barrel Jack: 2.1mm DC Barrel Jack with Thru-Hole Connectors (breadboardable)
